// Logisim project Project.circ as structural Verilog: 10 circuits, main circuit main
module main (
  input  [3:0] INPR
);

  wire clock_1_out;
  wire [3:0] AC_out_6, AR_out_6, DR_out_6, n4alu_1_out_14, OUTR_out_6, PC_out_6;
  wire [7:0] controlled_buffer_1_out, ram_1_data, undriven;

  _4ALU u_4alu_1 (
    .AC(AC_out_6), .DR(DR_out_6), .INPR(INPR), .out_14(n4alu_1_out_14));  // open: AND, ADD, CMA, LD_DR, LD_INPR, CIR, CIL, cin, E_AC_0, out_15, E_AC3
  _4Reg AR (.in_3(controlled_buffer_1_out[3:0]), .CLK(clock_1_out), .out_6(AR_out_6));  // open: LD, INC, CLR
  _4Reg PC (.in_3(controlled_buffer_1_out[3:0]), .CLK(clock_1_out), .out_6(PC_out_6));  // open: LD, INC, CLR
  _4Reg DR (.in_3(controlled_buffer_1_out[3:0]), .CLK(clock_1_out), .out_6(DR_out_6));  // open: LD, INC, CLR
  _4Reg AC (.in_3(n4alu_1_out_14), .CLK(clock_1_out), .out_6(AC_out_6));  // open: LD, INC, CLR
  _8Reg IR (.in_2(controlled_buffer_1_out), .CLK(clock_1_out), .in_1(undriven));  // open: LD, INC, CLR
  _4Reg OUTR (.in_3(controlled_buffer_1_out[3:0]), .CLK(clock_1_out), .out_6(OUTR_out_6));  // open: LD, INC, CLR
  Clock clock_1 (.out(clock_1_out));
  RAM #(.addrWidth(4), .bus("separate")) ram_1 (
    .addr(AR_out_6), .din(controlled_buffer_1_out), .data(ram_1_data), .clk(clock_1_out));  // open: str, sel, ld, clr
  // Probe on AR_out_6
  // Probe on PC_out_6
  // Probe on DR_out_6
  // Probe on AC_out_6
  // Probe on undriven
  // Probe on OUTR_out_6
  Controlled_Buffer #(.width(8)) controlled_buffer_1 (.in(ram_1_data), .out(controlled_buffer_1_out));  // open: en
  Controlled_Buffer #(.width(8)) controlled_buffer_2 (
    .in({4'b0000, AR_out_6}), .out(controlled_buffer_1_out));  // open: en
  Controlled_Buffer #(.width(8)) controlled_buffer_3 (
    .in({4'b0000, PC_out_6}), .out(controlled_buffer_1_out));  // open: en
  Controlled_Buffer #(.width(8)) controlled_buffer_4 (
    .in({4'b0000, DR_out_6}), .out(controlled_buffer_1_out));  // open: en
  Controlled_Buffer #(.width(8)) controlled_buffer_5 (
    .in({4'b0000, AC_out_6}), .out(controlled_buffer_1_out));  // open: en
  Controlled_Buffer #(.width(8)) controlled_buffer_6 (.in(undriven), .out(controlled_buffer_1_out));  // open: en
  // Probe on controlled_buffer_1_out
endmodule

module temp (
  input  D0,
  input  D1,
  input  D2,
  input  D3,
  input  D4,
  input  D5,
  input  D6,
  input  D7,
  input  D8,
  input  D9,
  input  D10,
  input  D11,
  input  D12,
  input  D13,
  input  D14,
  input  D15,
  input  T0,
  input  T1,
  input  T2,
  input  T3,
  input  T4
);

  wire ar_cont_1_ar_bus, ar_cont_1_ar_inc, ar_cont_1_ar_ld, dr_cont_1_dr_bus, dr_cont_1_dr_inc,
       dr_cont_1_dr_ld, ir_cont_1_ir_bus, ir_cont_1_ir_ld, pc_cont_1_pc_bus, pc_cont_1_pc_inc,
       pc_cont_1_pc_ld;
  wire [3:0] controlled_buffer_1_out, n4reg_1_out_6, n4reg_2_out_6, n4reg_3_out_6, n4reg_4_out_6;

  AR_Cont ar_cont_1 (
    .D4(D4), .D5(D5), .T0(T0), .T2(T2), .T3(T3), .T4(T4), .AR_BUS(ar_cont_1_ar_bus),
    .AR_INC(ar_cont_1_ar_inc), .AR_LD(ar_cont_1_ar_ld));
  PC_Cont pc_cont_1 (
    .D4(D4), .D5(D5), .D6(D6), .T0(T0), .T1(T1), .T3(T3), .T4(T4), .PC_BUS(pc_cont_1_pc_bus),
    .PC_INC(pc_cont_1_pc_inc), .PC_LD(pc_cont_1_pc_ld));
  DR_Cont dr_cont_1 (
    .D0(D0), .D1(D1), .D2(D2), .T3(T3), .T4(T4), .DR_BUS(dr_cont_1_dr_bus), .DR_INC(dr_cont_1_dr_inc),
    .DR_LD(dr_cont_1_dr_ld));
  IR_Cont ir_cont_1 (.T1(T1), .T2(T2), .IR_BUS(ir_cont_1_ir_bus), .IR_LD(ir_cont_1_ir_ld));
  _4Reg u_4reg_1 (
    .in_3(controlled_buffer_1_out), .LD(ar_cont_1_ar_ld), .INC(ar_cont_1_ar_inc), .out_6(n4reg_1_out_6));  // open: CLK, CLR
  _4Reg u_4reg_2 (
    .in_3(controlled_buffer_1_out), .LD(pc_cont_1_pc_ld), .INC(pc_cont_1_pc_inc), .out_6(n4reg_2_out_6));  // open: CLK, CLR
  _4Reg u_4reg_3 (
    .in_3(controlled_buffer_1_out), .LD(dr_cont_1_dr_ld), .INC(dr_cont_1_dr_inc), .out_6(n4reg_3_out_6));  // open: CLK, CLR
  _4Reg u_4reg_4 (.in_3(controlled_buffer_1_out), .LD(ir_cont_1_ir_ld), .out_6(n4reg_4_out_6));  // open: CLK, INC, CLR
  assign controlled_buffer_1_out = ar_cont_1_ar_bus ? n4reg_1_out_6 : 4'bz;  // Controlled_Buffer controlled_buffer_1
  assign controlled_buffer_1_out = pc_cont_1_pc_bus ? n4reg_2_out_6 : 4'bz;  // Controlled_Buffer controlled_buffer_2
  assign controlled_buffer_1_out = dr_cont_1_dr_bus ? n4reg_3_out_6 : 4'bz;  // Controlled_Buffer controlled_buffer_3
  assign controlled_buffer_1_out = ir_cont_1_ir_bus ? n4reg_4_out_6 : 4'bz;  // Controlled_Buffer controlled_buffer_4
endmodule

module _4Reg (
  input  INC,
  input  LD,
  input  [3:0] in_3,
  input  CLK,
  input  CLR,
  output [3:0] out_6
);

  wire and_1_out, and_2_out, and_3_out, and_4_out, and_5_out, and_6_out, and_7_out, and_8_out, and_9_out,
       and_10_out, and_11_out, and_12_out, not_1_out, not_2_out, not_3_out, not_4_out, not_5_out, not_6_out,
       or_1_out, or_2_out, or_3_out, or_4_out, or_5_out, or_6_out, or_7_out, or_8_out;

  not not_1 (not_1_out, LD);
  and and_1 (and_1_out, INC, not_1_out);
  not not_2 (not_2_out, not_1_out);
  not not_3 (not_3_out, in_3[0]);
  not not_4 (not_4_out, in_3[1]);
  not not_5 (not_5_out, in_3[2]);
  not not_6 (not_6_out, in_3[3]);
  and and_2 (and_2_out, not_2_out, in_3[0]);
  and and_3 (and_3_out, not_2_out, not_3_out);
  and and_4 (and_4_out, not_2_out, in_3[1]);
  and and_5 (and_5_out, not_2_out, not_4_out);
  and and_6 (and_6_out, not_2_out, in_3[2]);
  and and_7 (and_7_out, not_2_out, not_5_out);
  and and_8 (and_8_out, not_2_out, in_3[3]);
  and and_9 (and_9_out, not_2_out, not_6_out);
  and and_10 (and_10_out, and_1_out, out_6[0]);
  and and_11 (and_11_out, and_1_out, out_6[0], out_6[1]);
  and and_12 (and_12_out, and_1_out, out_6[0], out_6[1], out_6[2]);
  or or_1 (or_1_out, and_2_out, and_1_out);
  or or_2 (or_2_out, and_3_out, and_1_out);
  or or_3 (or_3_out, and_4_out, and_10_out);
  or or_4 (or_4_out, and_10_out, and_5_out);
  or or_5 (or_5_out, and_6_out, and_11_out);
  or or_6 (or_6_out, and_11_out, and_7_out);
  or or_7 (or_7_out, and_8_out, and_12_out);
  or or_8 (or_8_out, and_12_out, and_9_out);
  J_K_Flip_Flop j_k_ff_1 (.J(or_1_out), .clk(CLK), .K(or_2_out), .Q(out_6[0]), .reset(CLR));  // open: Qn, preset, en
  J_K_Flip_Flop j_k_ff_2 (.J(or_3_out), .clk(CLK), .K(or_4_out), .Q(out_6[1]), .reset(CLR));  // open: Qn, preset, en
  J_K_Flip_Flop j_k_ff_3 (.J(or_5_out), .clk(CLK), .K(or_6_out), .Q(out_6[2]), .reset(CLR));  // open: Qn, preset, en
  J_K_Flip_Flop j_k_ff_4 (.J(or_7_out), .clk(CLK), .K(or_8_out), .Q(out_6[3]), .reset(CLR));  // open: Qn, preset, en
endmodule

module _1ALU (
  input  INPR,
  input  DR,
  input  AC,
  input  AND,
  input  cin,
  input  ADD,
  input  CMA,
  input  LD_DR,
  input  LD_INPR,
  input  CIR,
  input  CIL,
  input  AC_i_1,
  input  AC_i_1_2,
  output cout,
  output output_AC
);

  wire add_out, adder_1_out, and_out, comp_out, Id_DR_out, Id_INPR_out, not_1_out, shl_out, shr_out;

  Adder #(.width(1)) adder_1 (.a(AC), .b(DR), .out(adder_1_out), .cin(cin), .cout(cout));
  not not_1 (not_1_out, AC);
  and u_and (and_out, AND, AC, DR);
  and u_add (add_out, ADD, adder_1_out);
  and comp (comp_out, CMA, not_1_out);
  and Id_DR (Id_DR_out, LD_DR, DR);
  and Id_INPR (Id_INPR_out, LD_INPR, INPR);
  and shl (shl_out, CIR, AC_i_1_2);
  and shr (shr_out, CIL, AC_i_1);
  or or_1 (output_AC, and_out, add_out, comp_out, Id_DR_out, Id_INPR_out, shl_out, shr_out);
endmodule

// ALU
module _4ALU (
  input  cin,
  input  [3:0] AC,
  input  E_AC_0,
  input  [3:0] DR,
  input  [3:0] INPR,
  input  AND,
  input  ADD,
  input  CMA,
  input  LD_DR,
  input  LD_INPR,
  input  CIR,
  input  CIL,
  input  E_AC3,
  output [3:0] out_14,
  output out_15
);

  wire n1alu_1_cout, n1alu_2_cout, n1alu_3_cout;

  _1ALU u_1alu_1 (
    .AND(AND), .ADD(ADD), .CMA(CMA), .LD_DR(LD_DR), .LD_INPR(LD_INPR), .CIR(CIR), .CIL(CIL), .AC_i_1(E_AC_0),
    .AC_i_1_2(AC[1]), .INPR(INPR[0]), .DR(DR[0]), .AC(AC[0]), .cin(cin), .cout(n1alu_1_cout),
    .output_AC(out_14[0]));
  _1ALU u_1alu_2 (
    .AND(AND), .ADD(ADD), .CMA(CMA), .LD_DR(LD_DR), .LD_INPR(LD_INPR), .CIR(CIR), .CIL(CIL), .AC_i_1(AC[0]),
    .AC_i_1_2(AC[2]), .INPR(INPR[1]), .DR(DR[1]), .AC(AC[1]), .cin(n1alu_1_cout), .cout(n1alu_2_cout),
    .output_AC(out_14[1]));
  _1ALU u_1alu_3 (
    .AND(AND), .ADD(ADD), .CMA(CMA), .LD_DR(LD_DR), .LD_INPR(LD_INPR), .CIR(CIR), .CIL(CIL), .AC_i_1(AC[1]),
    .AC_i_1_2(AC[3]), .INPR(INPR[2]), .DR(DR[2]), .AC(AC[2]), .cin(n1alu_2_cout), .cout(n1alu_3_cout),
    .output_AC(out_14[2]));
  _1ALU u_1alu_4 (
    .AND(AND), .ADD(ADD), .CMA(CMA), .LD_DR(LD_DR), .LD_INPR(LD_INPR), .CIR(CIR), .CIL(CIL), .AC_i_1(AC[2]),
    .AC_i_1_2(E_AC3), .INPR(INPR[3]), .DR(DR[3]), .AC(AC[3]), .cin(n1alu_3_cout), .cout(out_15),
    .output_AC(out_14[3]));
endmodule

module _8Reg (
  input  [7:0] in_1,
  input  [7:0] in_2,
  input  LD,
  input  CLR,
  input  INC,
  input  CLK
);

  _4Reg u_4reg_1 (.in_3(in_2[3:0]), .CLK(CLK), .LD(LD), .INC(INC), .CLR(CLR), .out_6(in_1[3:0]));
  _4Reg u_4reg_2 (.in_3(in_2[7:4]), .CLK(CLK), .LD(LD), .INC(INC), .CLR(CLR), .out_6(in_1[7:4]));
endmodule

module AR (
  input  D4,
  input  D5,
  input  T0,
  input  T2,
  input  T3,
  input  T4,
  output AR_BUS,
  output AR_INC,
  output AR_LD
);

  wire and_1_out, and_2_out;

  and and_1 (and_1_out, T3, D4);
  and and_2 (and_2_out, T4, D5);
  and and_3 (AR_INC, T3, D5);
  or or_1 (AR_LD, T2, T0);
  or or_2 (AR_BUS, and_1_out, and_2_out);
endmodule

module PC (
  input  D4,
  input  D5,
  input  D6,
  input  T0,
  input  T1,
  input  T3,
  input  T4,
  output PC_BUS,
  output PC_INC,
  output PC_LD
);

  wire and_1_out, and_2_out, and_3_out, and_4_out;

  and and_1 (and_1_out, D5, T3);
  and and_2 (and_2_out, D4, T3);
  and and_3 (and_3_out, D5, T4);
  and and_4 (and_4_out, D6, T3);
  or or_1 (PC_BUS, T0, and_1_out);
  or or_2 (PC_LD, and_2_out, and_3_out, and_4_out);

  assign PC_INC = T1;
endmodule

module DR (
  input  D0,
  input  D1,
  input  D2,
  input  T3,
  input  T4,
  output DR_BUS,
  output DR_INC,
  output DR_LD
);

  wire and_1_out, and_2_out, and_3_out, and_4_out, and_5_out, and_6_out;

  and and_1 (and_1_out, T4, D2);
  and and_2 (and_2_out, T4, D0);
  and and_3 (and_3_out, D1, T4);
  and and_4 (and_4_out, T3, D0);
  and and_5 (and_5_out, T3, D1);
  and and_6 (and_6_out, T3, D2);
  or or_1 (DR_BUS, and_1_out, and_2_out, and_3_out);
  or or_2 (DR_LD, and_4_out, and_5_out, and_6_out);
endmodule

module IR (
  input  T1,
  input  T2,
  output IR_BUS,
  output IR_LD
);


  assign IR_BUS = T2;
  assign IR_LD = T1;
endmodule
